# Fritzing sketch fritzing-board (saved by Fritzing 1.0.6)
breadboards: 1

parts:
  RHT2 = Humidity and Temperature Sensor RHT03
  HC-SR04_Sensor_1 = HC-SR04 Ultrasonic Distance Sensor
  L298N2 = L298N DC motor driver
  M2 = DC Motor [voltage_(max)=6V voltage_(min)=3V]
  LED1 = smd LED [color="Red (633nm)" package="0603 [SMD]"]
  R1 = Resistor [tolerance=±5% resistance=10 package="2010 [SMD]"]
  M3 = DC Motor [voltage_(max)=6V voltage_(min)=3V]
  M4 = DC Motor [voltage_(max)=6V voltage_(min)=3V]
  M5 = DC Motor [voltage_(max)=6V voltage_(min)=3V]
  R2 = Resistor [tolerance=±5% resistance=10 package="2010 [SMD]"]
  A2 = ESP32-S3-WROOM-1-N16R8 dev board
  YwRobot_Power_Supply2 = YwRobot Breadboard Power Supply [part_number=545043]
  VCC2 = 4 x AAA Battery Mount [internal_resistance=0.1Ω]
  U2 = LIPO-2000mAh [package=lipo-2000]  # not connected
  J1 = Piezo Speaker
  A3 = lcd color display 1.3in 240x240 7pin interface [package=THT]  # not connected

nets:
  VCC: RHT2.Vcc, HC-SR04_Sensor_1.VCC, R2.Pin_1, A2.Pin_1, A2.Pin_2, YwRobot_Power_Supply2.VCC#5, J1.pin1
  N1: RHT2.Data-signal, R2.Pin_0, A2.Pin_19
  N2: RHT2.GND_2, HC-SR04_Sensor_1.GND, R1.Pin_1, A2.Pin_22, A2.Pin_44, YwRobot_Power_Supply2.GND#11
  N3: HC-SR04_Sensor_1.TRIG, A2.Pin_9
  N4: HC-SR04_Sensor_1.ECHO, A2.Pin_10
  N5: L298N2.OUT1, M3.pin_2, M5.pin_2
  N6: L298N2.OUT2, M3.pin_1, M5.pin_1
  N7: L298N2.OUT3, M2.pin_1, M4.pin_1
  N8: L298N2.OUT4, M2.pin_2, M4.pin_2
  N9: L298N2.12V, VCC2.+
  N10: L298N2.GND, VCC2.-
  N11: L298N2.IN1, A2.Pin_28
  N12: L298N2.IN2, A2.Pin_29
  N13: L298N2.IN3, A2.Pin_30
  N14: L298N2.IN4, A2.Pin_32
  N15: LED1.cathode, R1.Pin_0
  N16: LED1.anode, A2.Pin_8
  N17: A2.Pin_20, J1.pin2
  N18: A2.Pin_21, YwRobot_Power_Supply2.GND#13

custom parts:
  L298N DC motor driver: 2x DC motor driver with 78M05 positive voltage regulator (7..35 V) L298N: max 46 V, 2 A Set 5 V Enable jumper to enable 5 V regultor (needed for the L298N) and +5 V output at screw terminal or supply external +5 V at screw terminal Set ENA and/or ENB to +5 V to enable motor permanently or supply ENA and/or ENB with PWM signal IN1 and IN2 set rotation directory for motor A (OUT1/OUT2) IN2 and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
  ESP32-S3-WROOM-1-N16R8 dev board: ESP32-S3 WIFI+BLE5.0 Development Board ESP32-S3-WROOM-1-N16R8(16M Flash/8SRAM).
  YwRobot Breadboard Power Supply: The YwRobot Breadboard Power Supply (MB-V2) has two power rails; they can be 5V or 3V3. Power to the module can be provided through the female USB socket or through the A10 (female) 2.1mm power jack.
  lcd color display 1.3in 240x240 7pin interface: 1.3 Inch Color 240 x 240 IPS TFT LCD Display Screen Module Board 7 Pin 4 Wire ST7789VW Drive IC SPI interface.
